# Fritzing sketch URC_v2.0 (saved by Fritzing 0.9.3b)

parts:
  Type_-_C = Arduino Nano (Rev3.0)
  JHD12864E_KS01 = 128 x 64 Graphic LCD
  Type-_C = ESP32-38PinWide [part_number=ESP32-38PinWide]
  8_4v_->_5_1v = LM2596 step down module
  Type_-_C_Booster_Module = 2S/3S stepup boost LIPO battery charger
  3_7v_Battery = battery_holder_single_18650
  3_7v_Battery_2 = battery_holder_single_18650
  Switch = SWITCH_SPDT [package=kps-1290]
  +ve = Resistor [tolerance=±5% resistance=100k package="0805 [SMD]"]
  -ve = Resistor [tolerance=±5% resistance=47k package="0805 [SMD]"]
  Analog_Reader_Module = Adafruit ADS1115 16-Bit ADC [part_number=1085]
  1000uf_Capacitor = Capacitor Polarized [package=cpol-radial-1000uf-25v]
  100uf_Capacitor = Capacitor Polarized [package=cpol-radial-100uf-25v]
  Left_Analog_Stick = Black Joystick KY-023
  Right_Analog_Stick = Black Joystick KY-023
  Left_Toggle_Switch = SWITCH_SPDT [package=kps-1290]
  Right_Toggle_Switch = SWITCH_SPDT [package=kps-1290]
  Left_Button = Round Pushbutton
  Right_Button = Round Pushbutton
  Ledt_Pot = Slide Potentiometer [maximum_resistance=100kΩ]
  Right_Pot = Slide Potentiometer [maximum_resistance=100kΩ]
  LED1 = DUO LED RG [package="5 mm [THT]"]
  -ve2 = Resistor [tolerance=±5% resistance=220 package="0805 [SMD]"]
  -ve3 = Resistor [tolerance=±5% resistance=220 package="0805 [SMD]"]

nets:
  N1: Type_-_C.D1/TX, Type-_C.GPIO16
  N2: Type_-_C.D0/RX, Type-_C.GPIO17
  GND: Type_-_C.GND, JHD12864E_KS01.1_Vss, JHD12864E_KS01.5_R/W, JHD12864E_KS01.20_K(-), Type-_C.GND, 8_4v_->_5_1v.IN-, 8_4v_->_5_1v.OUT-, Type_-_C_Booster_Module.Pin_4, Type_-_C_Booster_Module.Pin_5, 3_7v_Battery_2.+#0, -ve.Pin_0, Analog_Reader_Module.GND, 1000uf_Capacitor.-, 100uf_Capacitor.-, Left_Analog_Stick.GND, Right_Analog_Stick.GND, Left_Toggle_Switch.P, Right_Toggle_Switch.P, Left_Button.leg0, Right_Button.leg0, Ledt_Pot.leg2, Right_Pot.leg2
  N3: Type_-_C.D2, JHD12864E_KS01.7_DB0
  N4: Type_-_C.D3, JHD12864E_KS01.8_DB1
  N5: Type_-_C.D4, JHD12864E_KS01.9_BD2
  N6: Type_-_C.D5, JHD12864E_KS01.10_DB3
  N7: Type_-_C.D6, JHD12864E_KS01.11_DB4
  N8: Type_-_C.D7, JHD12864E_KS01.12_DB5
  N9: Type_-_C.D8, JHD12864E_KS01.13_DB6
  N10: Type_-_C.D9, JHD12864E_KS01.14_DB7
  N11: Type_-_C.D10, JHD12864E_KS01.15_CS1
  N12: Type_-_C.D11/MOSI, JHD12864E_KS01.16_CS2
  VIN: Type_-_C.VIN, Type-_C.VIN, 8_4v_->_5_1v.OUT+, 1000uf_Capacitor.+
  N13: Type_-_C.5V, JHD12864E_KS01.2_Vdd
  N14: Type_-_C.A5, JHD12864E_KS01.4_D/I
  N15: Type_-_C.A4, JHD12864E_KS01.6_Enable
  N16: Type_-_C.3V3, JHD12864E_KS01.19_A(+)
  +5V: Type-_C.3.3, Analog_Reader_Module.VCC, Left_Analog_Stick.+5V, Right_Analog_Stick.+5V, Ledt_Pot.leg1, Right_Pot.leg1, LED1.common_cathode
  N17: Type-_C.GPIO36, Right_Pot.wiper
  N18: Type-_C.GPIO39, Ledt_Pot.wiper
  N19: Type-_C.GPIO34, Right_Analog_Stick.VRy
  N20: Type-_C.GPIO35, Left_Analog_Stick.VRx
  N21: Type-_C.GPIO32, Left_Analog_Stick.VRy
  N22: Type-_C.GPIO33, Right_Analog_Stick.VRx
  N23: Type-_C.GPIO25, Left_Button.leg1
  N24: Type-_C.GPIO26, Left_Analog_Stick.SW
  N25: Type-_C.GPIO27, Right_Analog_Stick.SW
  N26: Type-_C.GPIO13, Right_Button.leg1
  N27: Type-_C.GPIO2, -ve3.Pin_1
  N28: Type-_C.GPIO4, -ve2.Pin_1
  N29: Type-_C.GPIO18, Right_Toggle_Switch.O
  N30: Type-_C.GPIO19, Left_Toggle_Switch.O
  N31: Type-_C.GPIO21, Analog_Reader_Module.SDA
  N32: Type-_C.GPIO22, Analog_Reader_Module.SCL
  N33: 8_4v_->_5_1v.IN+, Switch.P
  N34: Type_-_C_Booster_Module.Pin_1, Type_-_C_Booster_Module.Pin_2, 3_7v_Battery.+#1, Switch.S, +ve.Pin_0
  N35: 3_7v_Battery.+#0, 3_7v_Battery_2.+#1
  N36: +ve.Pin_1, -ve.Pin_1, Analog_Reader_Module.AIN0, 100uf_Capacitor.+
  N37: LED1.red_anode, -ve3.Pin_0
  N38: LED1.green_anode, -ve2.Pin_0

notes:
  VCC
  Y
  X
  GND
  BTN

custom parts:
  ESP32-38PinWide: Generic 38-Pin ESP32 with wide format (only access to one side of pins on a breadboard) based on Stephen Lilley's HiLetgo ESP-WROOM-32 ESP32 ESP-32S Development Board.
  LM2596 step down module: LM2596 DC-DC step down power supply module 3 A.
  2S/3S stepup boost LIPO battery charger: Type-C 2/3S Mini Li-Ion Battery Charging Module with QC Fast Charging Support with Charge Indicator Lights.
  battery_holder_single_18650: single 18650 battery holder
  Adafruit ADS1115 16-Bit ADC: For microcontrollers without an analog-to-digital converter or when you want a higher-precision ADC, the ADS1115 provides 16-bit precision at 860 samples/second over I2C. The chip can be configured as 4 single-ended input channels, or two differential channels. As a nice bonus, it even includes a programmable gain amplifier, up to x16, to help boost up smaller single/differential signals to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
  Black Joystick KY-023: Description: The joystick is a combination of 2 analoog potentiometer and a digital switch. Arduino GND --> Module pin - Arduino +5V --> Module pin +5V Arduino Analoog 0 --> Module VRx Arduino Analoog 1 --> Module VRy Arduino Digital --> Module SW Dimensions: 1" x 1.25"
