# Fritzing sketch Robo_Car_Rx (saved by Fritzing 0.9.3b)
circuit board: 8.46667cm x 5.64444cm

parts:
  3_7v_Charger = TP4056 [chip_label=TP4056 package="DIP (Dual Inline) [THT]"]
  ESP32-C3mini = Esp32-c3 super mini
  1 = Motor Driver 1A Dual TB6612FNG
  Left_Motor = DC Mini Metal Gear Motor
  Right_Motor = DC Mini Metal Gear Motor
  3_7v_Batt = Battery Holders [package=lipo-1100mAh]
  5v_Booster = DC-DC Power Module (5v)
  1000uf_25v = Capacitor Polarized [package=cpol-radial-100uf-25v]
  Switch = SWITCH_SPDT [package=kps-1290]

nets:
  N1: 3_7v_Charger.pin3, Switch.S
  N2: 3_7v_Charger.pin4, 3_7v_Batt.+
  N3: 3_7v_Charger.pin5, 3_7v_Batt.-
  N4: 3_7v_Charger.pin6, 5v_Booster.GND, 1000uf_25v.-
  N5: ESP32-C3mini.Pin_1, 1.BIN1
  N6: ESP32-C3mini.Pin_2, 1.BIN2
  N7: ESP32-C3mini.Pin_3, 1.PWMB
  N8: ESP32-C3mini.Pin_4, 1.STBY
  N9: ESP32-C3mini.Pin_11, 1.AIN1
  N10: ESP32-C3mini.Pin_12, 1.AIN2
  N11: ESP32-C3mini.Pin_13, 1.PWMA
  N12: ESP32-C3mini.Pin_14, 1.VCC
  N13: ESP32-C3mini.Pin_15, 1.GND, 5v_Booster.GND*
  N14: ESP32-C3mini.Pin_16, 1.VM, 5v_Booster.Vout
  N15: 1.B01, Left_Motor.IN1
  N16: 1.B02, Left_Motor.IN2
  N17: 1.A02, Right_Motor.IN1
  N18: 1.A01, Right_Motor.IN2
  N19: 5v_Booster.Vin, 1000uf_25v.+, Switch.P

notes:
  GND
  Vin

custom parts:
  TP4056: A DIP stand-in part for whatever IC you want. With 6 pins on a 300mil dual inline package (DIP) footprint.
  Esp32-c3 super mini: ESP32-C3 Development Board ESP32 SuperMini Development Board ESP32 Development Board WiFi Bluetooth.
  DC-DC Power Module (5v): DC-DC Power Module based con AMS1117-5.0 Input: DC 6~12V (input power must higher 1V than output power); Output: 5V (+/-0.05V error), 800mA
