# Fritzing sketch ESP_Controller_Rx_v0.9.3 (saved by Fritzing 0.9.3b)

parts:
  TB6612FNG = Pololu TB6612 motor driver
  Right_Wheel_Motor = DC Mini Metal Gear Motor
  Left_Wheel_Motor = DC Mini Metal Gear Motor
  Type-C = Esp32-c3 super mini
  3_7v_Charger = TP4056 [chip_label=TP4056 package="DIP (Dual Inline) [THT]"]
  3_7_Li-Ion_Battery = LIPO-2000mAh [package=lipo-2000]
  Switch = SWITCH_SPDT [package=kps-1290]
  ME2108A33P_3_7->5v = mini boost module
  Flap-up/Down = Basic Servo

nets:
  N1: TB6612FNG.Pin_1, TB6612FNG.Pin_9, Type-C.Pin_15, ME2108A33P_3_7->5v.Pin_3, Flap-up/Down.gnd
  N2: TB6612FNG.Pin_2, Type-C.Pin_14
  N3: TB6612FNG.Pin_3, Left_Wheel_Motor.IN1
  N4: TB6612FNG.Pin_4, Left_Wheel_Motor.IN2
  N5: TB6612FNG.Pin_5, Right_Wheel_Motor.IN2
  N6: TB6612FNG.Pin_6, Right_Wheel_Motor.IN1
  N7: TB6612FNG.Pin_7, Type-C.Pin_16, ME2108A33P_3_7->5v.Pin_4, Flap-up/Down.vcc
  N8: TB6612FNG.Pin_10, Type-C.Pin_3
  N9: TB6612FNG.Pin_11, Type-C.Pin_2
  N10: TB6612FNG.Pin_12, Type-C.Pin_1
  N11: TB6612FNG.Pin_13, Type-C.Pin_4
  N12: TB6612FNG.Pin_14, Type-C.Pin_11
  N13: TB6612FNG.Pin_15, Type-C.Pin_12
  N14: TB6612FNG.Pin_16, Type-C.Pin_13
  N15: Type-C.Pin_6, Flap-up/Down.pulse
  N16: 3_7v_Charger.pin3, Switch.S
  N17: 3_7v_Charger.pin4, 3_7_Li-Ion_Battery.+
  N18: 3_7v_Charger.pin5, 3_7_Li-Ion_Battery.-
  N19: 3_7v_Charger.pin6, ME2108A33P_3_7->5v.Pin_1
  N20: Switch.P, ME2108A33P_3_7->5v.Pin_2

custom parts:
  Pololu TB6612 motor driver: This tiny board is an easy way to use Toshiba’s TB6612FNG dual motor driver, which can independently control two bidirectional DC motors or one bipolar stepper motor.
  Esp32-c3 super mini: ESP32-C3 Development Board ESP32 SuperMini Development Board ESP32 Development Board WiFi Bluetooth.
  TP4056: A DIP stand-in part for whatever IC you want. With 6 pins on a 300mil dual inline package (DIP) footprint.
  mini boost module: mini boost module.
